# Fritzing sketch HW2 (saved by Fritzing 0.9.3b)
breadboards: 1

parts:
  Part1 = Arduino Nano (Rev3.0)
  R1 = Photocell (LDR) [package=THT]
  RE1 = Rotary Encoder [package=THT]
  R2 = Resistor [tolerance=±5% resistance=220 package=THT]
  S1 = Pushbutton [package="[THT]"]
  S2 = Pushbutton [package="[THT]"]
  R3 = Resistor [tolerance=±5% resistance=220 package=THT]
  R4 = Resistor [tolerance=±5% resistance=220 package=THT]

nets (from the schematic view):
  N1: Part1.GND, Part1.D13/SCK, RE1.EncoderPinA, R2.Pin_1, R3.Pin_1, R4.Pin_1
  N2: Part1.D10, S2.Pin_1, S2.Pin_2, R3.Pin_0
  N3: Part1.D11/MOSI, Part1.5V, Part1.A1, R1.pin_0, R2.Pin_0, S1.Pin_3, S1.Pin_4, S2.Pin_3, S2.Pin_4
  N4: Part1.D12/MISO, S1.Pin_1, S1.Pin_2, R4.Pin_0
  N5: Part1.A0, RE1.EncoderPinC
  N6: R1.pin_1, RE1.EncoderPinB
